# Fritzing sketch Esquemático (saved by Fritzing 0.9.3b)
breadboards: 1

parts:
  Raspberry_Pi_1 = Raspberry Pi 3 [part_number=RPI-3-V1.2]
  hc-sr2 = hc-sr04
  hc-sr3 = hc-sr04
  hc-sr1 = hc-sr04
  R1 = Resistor [tolerance=±5% resistance=1k package="2010 [SMD]"]
  R2 = Resistor [tolerance=±5% resistance=1k package="2010 [SMD]"]
  R3 = Resistor [tolerance=±5% resistance=1k package="2010 [SMD]"]
  R4 = Resistor [tolerance=±5% resistance=680 package="0402 [SMD]"]
  R5 = Resistor [tolerance=±5% resistance=680 package="0402 [SMD]"]
  R6 = Resistor [tolerance=±5% resistance=680 package="0402 [SMD]"]
  U1 = Nokia 6100 Color LCD [package=nokia6100_lcd]

nets:
  N1: Raspberry_Pi_1.3v3, U1.VDIGITAL
  N2: Raspberry_Pi_1.GPIO4, R2.Pin_1, R4.Pin_0
  N3: Raspberry_Pi_1.GPIO17, U1.DIO
  N4: Raspberry_Pi_1.GPIO11, U1.SCK
  N5: Raspberry_Pi_1.GPIO6, hc-sr2.Echo
  N6: Raspberry_Pi_1.GPIO13, R3.Pin_1, R6.Pin_0
  N7: Raspberry_Pi_1.GPIO19, hc-sr1.Echo
  N8: Raspberry_Pi_1.GPIO26, hc-sr3.Echo
  N9: Raspberry_Pi_1.GPIO16, R1.Pin_1, R5.Pin_0
  N10: Raspberry_Pi_1.GPIO8, U1.CS
  N11: Raspberry_Pi_1.GPIO24, U1.RESET
  GND: Raspberry_Pi_1.GND, hc-sr2.GND, hc-sr3.GND, hc-sr1.GND, R1.Pin_0, R2.Pin_0, R3.Pin_0, U1.GND, U1.LEDGND
  VCC: Raspberry_Pi_1.5V, hc-sr2.VCC, hc-sr3.VCC, hc-sr1.VCC
  N12: hc-sr2.Trig, R6.Pin_1
  N13: hc-sr3.Trig, R5.Pin_1
  N14: hc-sr1.Trig, R4.Pin_1
